# Fritzing sketch HungchoiPass-Pico (saved by Fritzing 0.9.3b)
circuit board: 7.18264cm x 3.37787cm

parts:
  Mod1 = Raspberry Pi Pico
  Part1 = RFID-RC522-v2
  Part2 = Bluetooth HC-05 Macho
  BAT1 = Battery Holders [package=lipo-1100mAh]
  Part3 = INA219 High Side DC Current Sensor Breakout [part_number=904]
  Part4 = PowerBoost 500 Charger

nets:
  N1: Mod1.pin_1, Part1.RST
  N2: Mod1.pin_2, Part1.SDA
  GND: Mod1.pin_3, Mod1.pin_13, Mod1.pin_18, Mod1.pin_33, Mod1.pin_38, Mod1.pin_42, Part1.GND, Part2.GND, BAT1.-, Part3.GND, Part4.GND
  N3: Mod1.pin_4, Part1.SCK
  N4: Mod1.pin_5, Part1.MOSI
  N5: Mod1.pin_6, Part1.MISO
  N6: Mod1.pin_16, Part2.TXD
  N7: Mod1.pin_17, Part2.RXD
  N8: Mod1.pin_19, Part3.SDA
  N9: Mod1.pin_20, Part3.SCL
  VCC: Mod1.pin_36, Part1.3.3V, Part2.VCC, Part3.VCC
  N10: Mod1.pin_37, BAT1.+, Part4.VBAT_OUT

custom parts:
  Raspberry Pi Pico: Raspberry Pi Pico. Based around the RP2040 microcontroller the Pico is a low cost microcontroller device bringing Raspberry Pi quality, cost, and easy of use to the microcontroller space. Jan 2021, Split part in to two versions: tht (this one) and SMD. This one will drill holes for a .1 in header in pcb to allow plugging in the module as well as providing pads to solder the module to the top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
  RFID-RC522-v2: A simple China made RFID-RC522 Reader; do check the pin labels, as this is a MFRC522 based clone.
  INA219 High Side DC Current Sensor Breakout: This breakout board will solve all your power-monitoring problems. Instead of struggling with two multimeters, you can just use the handy INA219B chip on this breakout to both measure both the high side voltage and DC current draw over I2C with 1% precision. Most current-measuring devices such as our current panel meter are only good for low side measuring. That means that unless you want to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
